// Logisim project Design.circ as structural Verilog
module Segment_Address_Decoding (
  input  K0,
  input  A4,
  input  K1,
  input  A5,
  input  K2,
  input  A6,
  input  K3,
  input  A7,
  output F
);

  wire nor_1_out, nor_2_out, nor_3_out, nor_4_out;

  nor nor_1 (nor_1_out, K0, A4);
  nor nor_2 (nor_2_out, K1, A5);
  nor nor_3 (nor_3_out, K2, A6);
  nor nor_4 (nor_4_out, K3, A7);
  and and_1 (F, nor_1_out, nor_2_out, nor_3_out, nor_4_out);

  // Notes on the sheet:
  //   F
endmodule
