// Logisim project 1_2.circ as structural Verilog: 1 circuit, main circuit main
module main (
  input  A,
  input  B,
  output S_Standard,
  output C_Carry
);

  xor xor_1 (S_Standard, A, B);
  and and_1 (C_Carry, A, B);

  // Notes on the sheet:
  //   addend
  //   augend
  //   1 bit Half Adder
endmodule
