// Logisim project 1_3.circ as structural Verilog: 1 circuit, main circuit main
module main (
  input  A,
  input  in_2,
  input  C,
  output S_Standard,
  output C_Carry
);

  wire and_1_out, and_2_out, xor_1_out;

  xor xor_1 (xor_1_out, A, in_2);
  and and_1 (and_1_out, A, in_2);
  xor xor_2 (S_Standard, xor_1_out, C);
  and and_2 (and_2_out, C, xor_1_out);
  or or_1 (C_Carry, and_2_out, and_1_out);

  // Notes on the sheet:
  //   Augend
  //   Addend
  //   CarryFromLowPositon
  //   B
  //   1 Bit Full Adder
endmodule
