// Logisim project 1_4.circ as structural Verilog: 2 circuits, main circuit main
module main (
  input  in_1,
  input  in_2,
  input  in_3,
  input  in_4,
  input  in_5,
  input  in_6,
  input  in_7,
  input  in_8,
  input  in_9,
  output S3,
  output S2,
  output S1,
  output S0,
  output C_Carry
);

  wire n1bitfulladder_2_c_carry, n1bitfulladder_3_c_carry, n1bitfulladder_4_c_carry;

  _1BitFullAdder u_1bitfulladder_1 (
    .A(in_2), .in_2(in_3), .C(n1bitfulladder_2_c_carry), .S_Standard(S3), .C_Carry(C_Carry));
  _1BitFullAdder u_1bitfulladder_2 (
    .A(in_4), .in_2(in_5), .C(n1bitfulladder_3_c_carry), .S_Standard(S2), .C_Carry(n1bitfulladder_2_c_carry));
  _1BitFullAdder u_1bitfulladder_3 (
    .A(in_6), .in_2(in_7), .C(n1bitfulladder_4_c_carry), .S_Standard(S1), .C_Carry(n1bitfulladder_3_c_carry));
  _1BitFullAdder u_1bitfulladder_4 (
    .A(in_8), .in_2(in_9), .C(in_1), .S_Standard(S0), .C_Carry(n1bitfulladder_4_c_carry));

  // Notes on the sheet:
  //   A3
  //   B3
  //   A2
  //   B2
  //   4 Bits Serial Carry Parallel Adder
  //   A1
  //   B1
  //   A0
  //   B0
  //   CarryFromLowPositon
endmodule

module _1BitFullAdder (
  input  A,
  input  in_2,
  input  C,
  output S_Standard,
  output C_Carry
);

  wire and_1_out, and_2_out, xor_1_out;

  xor xor_1 (xor_1_out, A, in_2);
  and and_1 (and_1_out, A, in_2);
  xor xor_2 (S_Standard, xor_1_out, C);
  and and_2 (and_2_out, C, xor_1_out);
  or or_1 (C_Carry, and_2_out, and_1_out);

  // Notes on the sheet:
  //   Augend
  //   Addend
  //   CarryFromLowPositon
  //   B
  //   1 Bit Full Adder
endmodule
