// Logisim project 2_3.circ as structural Verilog: 10 circuits, main circuit 4-Bit Reversible Counter
module _4_Bit_Reversible_Counter (
  input  CLR,
  input  CPD,
  input  CPU,
  output Q3,
  output Q2,
  output Q1,
  output Q0
);

  wire and_1_out, and_2_out, and_3_out, and_4_out, and_5_out, and_6_out, D0_qn, D1_qn, D2_qn, D3_qn,
       or_1_out, or_2_out, or_3_out, or_4_out;

  or or_1 (or_1_out, and_1_out, and_2_out);
  and and_1 (and_1_out, D0_qn, D1_qn, D2_qn, CPD);
  D_Flip_Flop #(.trigger("falling")) D3 (
    .clk(or_1_out), .D(D3_qn), .Q(Q3), .Qn(D3_qn), .preset(1'b0), .en(1'b1), .reset(CLR));
  and and_2 (and_2_out, Q2, Q1, Q0, CPU);
  and and_3 (and_3_out, D0_qn, D1_qn, CPD);
  or or_2 (or_2_out, and_3_out, and_4_out);
  and and_4 (and_4_out, Q0, Q1, CPU);
  D_Flip_Flop #(.trigger("falling")) D2 (
    .clk(or_2_out), .D(D2_qn), .Q(Q2), .Qn(D2_qn), .preset(1'b0), .en(1'b1), .reset(CLR));
  and and_5 (and_5_out, D0_qn, CPD);
  or or_3 (or_3_out, and_5_out, and_6_out);
  and and_6 (and_6_out, Q0, CPU);
  D_Flip_Flop #(.trigger("falling")) D1 (
    .clk(or_3_out), .D(D1_qn), .Q(Q1), .Qn(D1_qn), .preset(1'b0), .en(1'b1), .reset(CLR));
  or or_4 (or_4_out, CPD, CPU);
  D_Flip_Flop #(.trigger("falling")) D0 (
    .clk(or_4_out), .D(D0_qn), .Q(Q0), .Qn(D0_qn), .preset(1'b0), .en(1'b1), .reset(CLR));

  // Notes on the sheet:
  //   Q3
  //   Q2
  //   Q1
  //   Q0
  //   4-Bit Reversible Counter
  //   /Q3
  //   /Q2
  //   /Q1
  //   /Q0
endmodule

module _4_Bit_Reversible_Counter_Test (
  input  in_1,
  output out_2,
  output out_3,
  output out_4,
  output out_5
);

  wire button_1_out, button_2_out;

  Button button_1 (.out(button_1_out));
  Button button_2 (.out(button_2_out));
  _4_Bit_Reversible_Counter u_4_bit_reversible_counter_1 (
    .CLR(in_1), .CPU(button_2_out), .Q3(out_2), .Q2(out_3), .Q1(out_4), .Q0(out_5), .CPD(button_1_out));

  // Notes on the sheet:
  //   4-Bit Reversible Counter Test
endmodule

module HexadecimalTo8421 (
  input  H3,
  input  H2,
  input  H1,
  input  H0,
  output Y3,
  output Y2,
  output Y1,
  output Y0,
  output Y7,
  output Y6,
  output Y5,
  output Y4
);

  wire and_2_out, and_3_out, and_4_out, and_5_out, and_6_out, and_7_out, and_8_out, and_9_out, main_1_s0,
       main_1_s1, main_1_s2, main_1_s3, not_1_out, or_1_out;

  not not_1 (not_1_out, Y4);
  and and_1 (Y4, or_1_out, H3);
  or or_1 (or_1_out, H2, H1);
  _1_5_main main_1 (
    .S0(main_1_s0), .S1(main_1_s1), .S2(main_1_s2), .S3(main_1_s3), .C0FromLowPosition(1'b1), .A0(H0),
    .B0(1'b1), .A1(H1), .B1(1'b0), .A2(H2), .B2(1'b1), .A3(H3), .B3(1'b0));  // open: C4_Carry
  or or_2 (Y3, and_2_out, and_3_out);
  and and_2 (and_2_out, not_1_out, H3);
  and and_3 (and_3_out, Y4, main_1_s3);
  and and_4 (and_4_out, not_1_out, H2);
  or or_3 (Y2, and_4_out, and_5_out);
  and and_5 (and_5_out, Y4, main_1_s2);
  or or_4 (Y1, and_6_out, and_7_out);
  and and_6 (and_6_out, not_1_out, H1);
  and and_7 (and_7_out, Y4, main_1_s1);
  or or_5 (Y0, and_9_out, and_8_out);
  and and_8 (and_8_out, Y4, main_1_s0);
  and and_9 (and_9_out, not_1_out, H0);

  assign Y5 = 1'b0;
  assign Y6 = 1'b0;
  assign Y7 = 1'b0;

  // Notes on the sheet:
  //   H3
  //   H2
  //   H1
  //   H0
  //   HeadecimalTo8421
endmodule

module HexadecimalTo8421Test (
  input  in_1,
  input  in_2,
  input  in_3,
  input  in_4,
  output out_5,
  output out_6,
  output out_7,
  output out_8,
  output out_9,
  output out_10,
  output out_11,
  output out_12
);

  HexadecimalTo8421 hexadecimalto8421_1 (
    .Y7(out_5), .Y6(out_6), .Y5(out_7), .Y4(out_8), .Y3(out_9), .Y2(out_10), .Y1(out_11), .Y0(out_12),
    .H3(in_1), .H2(in_2), .H1(in_3), .H0(in_4));

  // Notes on the sheet:
  //   Hexadecimal To 8421 Test
endmodule

module _7_Segment_Decoder (
  input  A3,
  input  A2,
  input  A1,
  input  A0,
  output a,
  output b,
  output c,
  output d,
  output e,
  output f,
  output g
);

  wire and_1_out, and_2_out, and_3_out, and_4_out, and_5_out, and_6_out, and_7_out, and_8_out, and_9_out,
       and_10_out, and_11_out, and_12_out, and_13_out, and_14_out, and_15_out, and_16_out, and_17_out,
       and_18_out, and_19_out, and_20_out, and_21_out, and_22_out, and_23_out, and_24_out, and_25_out,
       not_1_out, not_2_out, not_3_out, not_4_out;

  not not_1 (not_1_out, A3);
  not not_2 (not_2_out, A2);
  not not_3 (not_3_out, A1);
  not not_4 (not_4_out, A0);
  and and_1 (and_1_out, not_1_out, not_2_out, not_4_out);
  or or_1 (a, and_1_out, and_3_out, and_2_out, and_4_out);
  and and_2 (and_2_out, A2, not_3_out, A0);
  and and_3 (and_3_out, not_1_out, A1, A0);
  and and_4 (and_4_out, A3, not_2_out, not_3_out);
  and and_5 (and_5_out, not_1_out, A1, A0);
  or or_2 (b, and_5_out, and_7_out, and_6_out, and_8_out);
  and and_6 (and_6_out, not_2_out, not_3_out);
  and and_7 (and_7_out, not_3_out, not_4_out);
  and and_8 (and_8_out, not_1_out, not_2_out);
  and and_9 (and_9_out, not_1_out, A2);
  or or_3 (c, and_9_out, and_10_out, and_11_out);
  and and_10 (and_10_out, not_2_out, not_3_out);
  and and_11 (and_11_out, not_2_out, A0);
  and and_12 (and_12_out, A2, not_3_out, A0);
  and and_13 (and_13_out, not_2_out, not_4_out);
  or or_4 (d, and_12_out, and_13_out, and_14_out, and_15_out);
  and and_14 (and_14_out, A1, not_4_out);
  and and_15 (and_15_out, not_2_out, A1);
  or or_5 (e, and_17_out, and_16_out);
  and and_16 (and_16_out, not_2_out, not_4_out);
  and and_17 (and_17_out, A1, not_4_out);
  and and_18 (and_18_out, not_3_out, not_4_out);
  or or_6 (f, and_18_out, and_19_out, and_21_out, and_20_out);
  and and_19 (and_19_out, A2, not_4_out);
  and and_20 (and_20_out, A3, not_3_out);
  and and_21 (and_21_out, A2, not_3_out);
  and and_22 (and_22_out, not_2_out, A1);
  or or_7 (g, and_22_out, and_23_out, and_24_out, and_25_out);
  and and_23 (and_23_out, A2, not_3_out);
  and and_24 (and_24_out, A2, not_4_out);
  and and_25 (and_25_out, A3, not_2_out);

  // Notes on the sheet:
  //   7 Segment Decoder
endmodule

module _7_Segment_Decoder_Test (
  input  in_1,
  input  in_2,
  input  in_3,
  input  in_4
);

  wire n7_segment_decoder_1_a, n7_segment_decoder_1_b, n7_segment_decoder_1_c, n7_segment_decoder_1_d,
       n7_segment_decoder_1_e, n7_segment_decoder_1_f, n7_segment_decoder_1_g;

  _7_Segment_Decoder u_7_segment_decoder_1 (
    .A3(in_1), .A2(in_2), .A1(in_3), .A0(in_4), .a(n7_segment_decoder_1_a), .b(n7_segment_decoder_1_b),
    .c(n7_segment_decoder_1_c), .d(n7_segment_decoder_1_d), .e(n7_segment_decoder_1_e),
    .f(n7_segment_decoder_1_f), .g(n7_segment_decoder_1_g));
  _7_Segment_Display u_7_segment_display_1 (
    .g(n7_segment_decoder_1_g), .f(n7_segment_decoder_1_f), .a(n7_segment_decoder_1_a),
    .b(n7_segment_decoder_1_b), .e(n7_segment_decoder_1_e), .d(n7_segment_decoder_1_d),
    .c(n7_segment_decoder_1_c), .dp(1'b0));

  // Notes on the sheet:
  //   7 Segment Decoder Test
endmodule

module _7_Segment_Decoder_Auto (
  input  A3,
  input  A2,
  input  A1,
  input  A0,
  output a,
  output b,
  output c,
  output d,
  output e,
  output f,
  output g
);

  wire and_1_out, and_2_out, and_3_out, and_4_out, and_5_out, and_6_out, and_7_out, and_8_out, and_9_out,
       and_10_out, and_11_out, and_12_out, and_13_out, and_14_out, and_15_out, and_16_out, and_17_out,
       and_18_out, and_19_out, and_20_out, and_21_out, and_22_out, and_23_out, and_24_out, and_25_out,
       and_26_out, not_1_out, not_2_out, not_3_out, not_4_out, not_5_out, not_6_out, not_7_out, not_8_out,
       not_9_out, not_10_out, not_11_out, not_12_out, not_13_out, not_14_out, not_15_out, not_16_out,
       not_17_out, not_18_out, not_19_out, not_20_out, not_21_out, not_22_out, not_23_out, not_24_out,
       not_25_out, not_26_out, not_27_out, not_28_out, not_29_out, not_30_out, not_31_out, not_32_out,
       not_33_out, not_34_out, not_35_out, not_36_out, not_37_out;

  not not_1 (not_1_out, A3);
  and and_1 (and_1_out, not_1_out, not_2_out, not_3_out);
  not not_2 (not_2_out, A2);
  not not_3 (not_3_out, A0);
  not not_4 (not_4_out, A3);
  and and_2 (and_2_out, not_4_out, not_5_out, A1);
  not not_5 (not_5_out, A2);
  not not_6 (not_6_out, A3);
  and and_3 (and_3_out, not_6_out, A2, A0);
  and and_4 (and_4_out, A3, not_7_out, not_8_out);
  not not_7 (not_7_out, A2);
  not not_8 (not_8_out, A1);
  not not_9 (not_9_out, A1);
  and and_5 (and_5_out, A3, not_9_out, A0);
  not not_10 (not_10_out, A3);
  and and_6 (and_6_out, not_10_out, not_11_out);
  not not_11 (not_11_out, A2);
  not not_12 (not_12_out, A2);
  and and_7 (and_7_out, not_12_out, not_13_out);
  not not_13 (not_13_out, A1);
  not not_14 (not_14_out, A1);
  and and_8 (and_8_out, not_14_out, not_15_out);
  not not_15 (not_15_out, A0);
  not not_16 (not_16_out, A3);
  and and_9 (and_9_out, not_16_out, A1, A0);
  not not_17 (not_17_out, A2);
  and and_10 (and_10_out, not_17_out, not_18_out);
  not not_18 (not_18_out, A1);
  not not_19 (not_19_out, A2);
  and and_11 (and_11_out, not_19_out, A0);
  not not_20 (not_20_out, A3);
  and and_12 (and_12_out, not_20_out, A2);
  not not_21 (not_21_out, A2);
  and and_13 (and_13_out, not_21_out, not_22_out);
  not not_22 (not_22_out, A0);
  not not_23 (not_23_out, A2);
  and and_14 (and_14_out, not_23_out, A1);
  and and_15 (and_15_out, A1, not_24_out);
  not not_24 (not_24_out, A0);
  and and_16 (and_16_out, A2, not_25_out, A0);
  not not_25 (not_25_out, A1);
  not not_26 (not_26_out, A2);
  and and_17 (and_17_out, not_26_out, not_27_out);
  not not_27 (not_27_out, A0);
  and and_18 (and_18_out, A1, not_28_out);
  not not_28 (not_28_out, A0);
  not not_29 (not_29_out, A1);
  and and_19 (and_19_out, not_29_out, not_30_out);
  not not_30 (not_30_out, A0);
  and and_20 (and_20_out, A2, not_31_out);
  not not_31 (not_31_out, A1);
  and and_21 (and_21_out, A2, not_32_out);
  not not_32 (not_32_out, A0);
  and and_22 (and_22_out, A3, not_33_out);
  not not_33 (not_33_out, A1);
  not not_34 (not_34_out, A2);
  and and_23 (and_23_out, not_34_out, A1);
  and and_24 (and_24_out, A2, not_35_out);
  not not_35 (not_35_out, A1);
  and and_25 (and_25_out, A2, not_36_out);
  not not_36 (not_36_out, A0);
  and and_26 (and_26_out, A3, not_37_out);
  not not_37 (not_37_out, A2);
  or or_1 (a, and_1_out, and_2_out, and_3_out, and_4_out, and_5_out);
  or or_2 (b, and_6_out, and_7_out, and_8_out, and_9_out);
  or or_3 (c, and_10_out, and_11_out, and_12_out);
  or or_4 (d, and_13_out, and_14_out, and_15_out, and_16_out);
  or or_5 (e, and_17_out, and_18_out);
  or or_6 (f, and_19_out, and_20_out, and_21_out, and_22_out);
  or or_7 (g, and_23_out, and_24_out, and_25_out, and_26_out);
endmodule

module Alarm (
  input  CLR,
  input  CPD,
  input  CPU,
  output Q3,
  output Q2,
  output Q1,
  output Q0,
  output Alarm
);

  wire and_2_out, and_3_out, not_1_out, or_1_out;

  or or_1 (or_1_out, Q3, Q2, Q1, Q0);
  and and_1 (Alarm, Q3, Q2, Q1, Q0);
  not not_1 (not_1_out, Alarm);
  and and_2 (and_2_out, or_1_out, CPD);
  and and_3 (and_3_out, not_1_out, CPU);
  _4_Bit_Reversible_Counter u_4_bit_reversible_counter_1 (
    .CLR(CLR), .CPU(and_3_out), .Q3(Q3), .Q2(Q2), .Q1(Q1), .Q0(Q0), .CPD(and_2_out));

  // Notes on the sheet:
  //   4-Bit Areversible Counter With Alarm
endmodule

module Alarm_Test (
  input  in_1,
  output out_2,
  output out_3,
  output out_4,
  output out_5
);

  wire alarm_1_alarm, button_1_out, button_2_out;

  Button button_1 (.out(button_1_out));
  Button button_2 (.out(button_2_out));
  Alarm alarm_1 (
    .CLR(in_1), .CPD(button_1_out), .CPU(button_2_out), .Q3(out_2), .Q2(out_3), .Q1(out_4), .Q0(out_5),
    .Alarm(alarm_1_alarm));
  LED led_1 (.in(alarm_1_alarm));

  // Notes on the sheet:
  //   Alarm Test
endmodule

module Access_Control_System (
  input  CLR
);

  wire alarm_1_alarm, alarm_1_q0, alarm_1_q1, alarm_1_q2, alarm_1_q3, button_1_out, button_2_out,
       hexadecimalto8421_1_y0, hexadecimalto8421_1_y1, hexadecimalto8421_1_y2, hexadecimalto8421_1_y3,
       hexadecimalto8421_1_y4, hexadecimalto8421_1_y5, hexadecimalto8421_1_y6, hexadecimalto8421_1_y7,
       n7_segment_decoder_1_a, n7_segment_decoder_1_b, n7_segment_decoder_1_c, n7_segment_decoder_1_d,
       n7_segment_decoder_1_e, n7_segment_decoder_1_f, n7_segment_decoder_1_g, n7_segment_decoder_2_a,
       n7_segment_decoder_2_b, n7_segment_decoder_2_c, n7_segment_decoder_2_d, n7_segment_decoder_2_e,
       n7_segment_decoder_2_f, n7_segment_decoder_2_g;

  _7_Segment_Decoder u_7_segment_decoder_1 (
    .A3(hexadecimalto8421_1_y7), .A2(hexadecimalto8421_1_y6), .A1(hexadecimalto8421_1_y5),
    .A0(hexadecimalto8421_1_y4), .a(n7_segment_decoder_1_a), .b(n7_segment_decoder_1_b),
    .c(n7_segment_decoder_1_c), .d(n7_segment_decoder_1_d), .e(n7_segment_decoder_1_e),
    .f(n7_segment_decoder_1_f), .g(n7_segment_decoder_1_g));
  Button button_1 (.out(button_1_out));
  Button button_2 (.out(button_2_out));
  _7_Segment_Display u_7_segment_display_1 (
    .g(n7_segment_decoder_1_g), .f(n7_segment_decoder_1_f), .a(n7_segment_decoder_1_a),
    .b(n7_segment_decoder_1_b), .e(n7_segment_decoder_1_e), .d(n7_segment_decoder_1_d),
    .c(n7_segment_decoder_1_c), .dp(1'b0));
  HexadecimalTo8421 hexadecimalto8421_1 (
    .Y7(hexadecimalto8421_1_y7), .Y6(hexadecimalto8421_1_y6), .Y5(hexadecimalto8421_1_y5),
    .Y4(hexadecimalto8421_1_y4), .Y3(hexadecimalto8421_1_y3), .Y2(hexadecimalto8421_1_y2),
    .Y1(hexadecimalto8421_1_y1), .Y0(hexadecimalto8421_1_y0), .H3(alarm_1_q3), .H2(alarm_1_q2),
    .H1(alarm_1_q1), .H0(alarm_1_q0));
  Alarm alarm_1 (
    .CLR(CLR), .CPD(button_1_out), .CPU(button_2_out), .Q3(alarm_1_q3), .Q2(alarm_1_q2), .Q1(alarm_1_q1),
    .Q0(alarm_1_q0), .Alarm(alarm_1_alarm));
  _7_Segment_Decoder u_7_segment_decoder_2 (
    .A3(hexadecimalto8421_1_y3), .A2(hexadecimalto8421_1_y2), .A1(hexadecimalto8421_1_y1),
    .A0(hexadecimalto8421_1_y0), .a(n7_segment_decoder_2_a), .b(n7_segment_decoder_2_b),
    .c(n7_segment_decoder_2_c), .d(n7_segment_decoder_2_d), .e(n7_segment_decoder_2_e),
    .f(n7_segment_decoder_2_f), .g(n7_segment_decoder_2_g));
  _7_Segment_Display u_7_segment_display_2 (
    .g(n7_segment_decoder_2_g), .f(n7_segment_decoder_2_f), .a(n7_segment_decoder_2_a),
    .b(n7_segment_decoder_2_b), .e(n7_segment_decoder_2_e), .d(n7_segment_decoder_2_d),
    .c(n7_segment_decoder_2_c), .dp(1'b0));
  LED led_1 (.in(alarm_1_alarm));

  // Notes on the sheet:
  //   Access Control System
endmodule
