// Logisim project 1_5.circ as structural Verilog: 2 circuits, main circuit main
module main (
  input  C0FromLowPosition,
  input  A0,
  input  B0,
  input  A1,
  input  B1,
  input  A2,
  input  B2,
  input  A3,
  input  B3,
  output S0,
  output S1,
  output S2,
  output S3,
  output C4_Carry
);

  wire and_1_out, and_2_out, and_3_out, and_4_out, and_5_out, and_6_out, and_7_out, and_8_out, or_1_out,
       or_2_out, or_3_out, or_5_out, or_6_out, or_7_out, or_8_out, xor_5_out, xor_6_out, xor_7_out, xor_8_out;

  xor xor_1 (S0, C0FromLowPosition, xor_5_out);
  xor xor_2 (S1, or_2_out, xor_6_out);
  xor xor_3 (S2, or_1_out, xor_7_out);
  xor xor_4 (S3, or_3_out, xor_8_out);
  LED C0 (.in(C0FromLowPosition));
  LED C1 (.in(or_2_out));
  LED C2 (.in(or_1_out));
  LED C3 (.in(or_3_out));
  xor xor_5 (xor_5_out, A0, B0);
  xor xor_6 (xor_6_out, A1, B1);
  or or_1 (or_1_out, and_1_out, and_6_out);
  xor xor_7 (xor_7_out, A2, B2);
  xor xor_8 (xor_8_out, A3, B3);
  and and_1 (and_1_out, or_2_out, or_6_out);
  or or_2 (or_2_out, and_2_out, and_5_out);
  or or_3 (or_3_out, and_3_out, and_7_out);
  or or_4 (C4_Carry, and_4_out, and_8_out);
  and and_2 (and_2_out, C0FromLowPosition, or_5_out);
  and and_3 (and_3_out, or_1_out, or_7_out);
  and and_4 (and_4_out, or_3_out, or_8_out);
  or or_5 (or_5_out, A0, B0);
  and and_5 (and_5_out, A0, B0);
  and and_6 (and_6_out, A1, B1);
  or or_6 (or_6_out, A1, B1);
  and and_7 (and_7_out, A2, B2);
  or or_7 (or_7_out, A2, B2);
  and and_8 (and_8_out, A3, B3);
  or or_8 (or_8_out, A3, B3);

  // Notes on the sheet:
  //   4 bit Look-Ahead Carry Parallel Carry Adder
endmodule

module test (
  input  in_1,
  input  in_2,
  input  in_3,
  input  in_4,
  input  in_5,
  input  in_6,
  input  in_7,
  input  in_8,
  input  in_9,
  output out_10,
  output out_11,
  output out_12,
  output out_13,
  output out_14
);

  main main_1 (
    .S0(out_13), .S1(out_12), .S2(out_11), .S3(out_10), .C4_Carry(out_14), .C0FromLowPosition(in_1),
    .A0(in_5), .B0(in_9), .A1(in_4), .B1(in_8), .A2(in_3), .B2(in_7), .A3(in_2), .B3(in_6));
endmodule
